# Fritzing sketch Fliper 2 (saved by Fritzing 0.9.3b)

parts:
  Pro_Micro3 = Pro Micro
  BUTTON2 = Arcade Button (green)
  BUTTON3 = Arcade Button (green)
  BUTTON4 = Arcade Button (green)
  BUTTON5 = Arcade Button (green)
  BUTTON6 = Arcade Button (blue)
  BUTTON7 = Arcade Button (blue)
  BUTTON8 = Arcade Button (blue)
  BUTTON9 = Arcade Button (blue)
  BUTTON12 = Arcade Button (green)
  BUTTON13 = Arcade Button (green)
  BUTTON16 = Arcade Button (green)
  BUTTON17 = Arcade Button (green)
  R1 = Rotary Potentiometer (Small) [maximum_resistance=100kΩ package=THT]
  R3 = Rotary Potentiometer (Small) [maximum_resistance=100kΩ package=THT]
  R5 = Rotary Potentiometer (Small) [maximum_resistance=100kΩ package=THT]
  R7 = Rotary Potentiometer (Small) [maximum_resistance=100kΩ package=THT]

nets:
  N1: Pro_Micro3.GND#3, R1.leg2, R3.leg2, R5.leg2, R7.leg2
  N2: Pro_Micro3.GND#4, BUTTON2.no_name_yet#1, BUTTON3.no_name_yet#1, BUTTON4.no_name_yet#1, BUTTON5.no_name_yet#1, BUTTON6.no_name_yet#1, BUTTON7.no_name_yet#1, BUTTON8.no_name_yet#1, BUTTON9.no_name_yet#1, BUTTON12.no_name_yet#1, BUTTON13.no_name_yet#1, BUTTON16.no_name_yet#1, BUTTON17.no_name_yet#1
  N3: Pro_Micro3.D2, BUTTON5.no_name_yet#2
  N4: Pro_Micro3.D3, BUTTON4.no_name_yet#2
  N5: Pro_Micro3.D4, BUTTON3.no_name_yet#2
  N6: Pro_Micro3.D5, BUTTON2.no_name_yet#2
  N7: Pro_Micro3.D6, BUTTON8.no_name_yet#2
  N8: Pro_Micro3.D7, BUTTON9.no_name_yet#2
  N9: Pro_Micro3.D8, BUTTON7.no_name_yet#2
  N10: Pro_Micro3.D9, BUTTON6.no_name_yet#2
  N11: Pro_Micro3.D10, BUTTON16.no_name_yet#2
  N12: Pro_Micro3.D16/MOSI, BUTTON12.no_name_yet#2
  N13: Pro_Micro3.D14/MISO, BUTTON17.no_name_yet#2
  N14: Pro_Micro3.D15/SCLK, BUTTON13.no_name_yet#2
  N15: Pro_Micro3.D18/A0, R5.wiper
  N16: Pro_Micro3.D19/A1, R3.wiper
  N17: Pro_Micro3.D20/A2, R1.wiper
  N18: Pro_Micro3.D21/A3, R7.wiper
  N19: Pro_Micro3.VCC, R1.leg1, R3.leg1, R5.leg1, R7.leg1

notes:
  DIY MIDI Controller
  by Gustavo Silveira
  www.musiconerd.com
  gustavosilveira@musiconerd.com
  Arduino Pro Micro

custom parts:
  Pro Micro: The SparkFun Pro Micro is a complete USB-based microcontoller development system, in a very small footprint, capable of implementing many types of projects. All programming can be done via the USB port.
  Arcade Button (green): Adafruit Arcade Button (green)
  Arcade Button (blue): Adafruit Arcade Button (blue)
